// Logisim project project.circ as structural Verilog: 1 circuit, main circuit main
module main (
  input  S0,
  input  S1,
  input  S3,
  input  S2,
  input  RESET,
  output FULL,
  output pump,
  output Alarm
);

  wire and_1_out, CLK, not_1_out, not_2_out, not_3_out, not_4_out, not_5_out, not_6_out, or_1_out, or_2_out,
       or_3_out, or_4_out, or_5_out, REG_L0, REG_L1;
  wire [1:0] counter_1_q;

  not not_1 (not_1_out, REG_L0);
  not not_2 (not_2_out, REG_L0);
  not not_3 (not_3_out, REG_L1);
  not not_4 (not_4_out, REG_L0);
  not not_5 (not_5_out, REG_L1);
  or or_1 (or_1_out, S1, S3);
  Clock clock_1 (.out(CLK));
  or or_2 (or_2_out, REG_L1, not_1_out);
  and and_1 (and_1_out, not_2_out, not_3_out);
  not not_6 (not_6_out, REG_L0);
  or or_3 (or_3_out, REG_L1, not_4_out);
  or or_4 (or_4_out, not_5_out, REG_L0);
  or or_5 (or_5_out, S3, S2);
  _7_Segment_Display u_7_segment_display_1 (
    .g(REG_L1), .f(and_1_out), .a(or_2_out), .b(1'b1), .e(not_6_out), .d(or_3_out), .c(or_4_out));  // open: dp
  D_Flip_Flop d_ff_1 (.clk(CLK), .D(or_1_out), .Q(REG_L0));  // open: Qn, preset, en, reset
  D_Flip_Flop d_ff_2 (.clk(CLK), .D(or_5_out), .Q(REG_L1));  // open: Qn, preset, en, reset
  and and_2 (FULL, or_1_out, or_5_out);
  Counter #(.width(2), .max('h3)) counter_1 (
    .count(FULL), .Q(counter_1_q), .clk(CLK), .clr(RESET));  // open: load, D, carry
  not not_7 (pump, FULL);
  and and_3 (Alarm, counter_1_q[0], counter_1_q[1]);
endmodule
